# Fritzing sketch layout (saved by Fritzing 1.0.1rc)
breadboards: 1

parts:
  NodeMCU_ESP32 = ESP32 DOIT DEVKIT V1 36pin
  5V_DC_Fan = Small Fan, based on Fan - Ventilador [package=THT]
  BME280_Breakout = BME280

nets:
  GND: NodeMCU_ESP32.Pin_17, 5V_DC_Fan.GND, BME280_Breakout.GND
  N1: NodeMCU_ESP32.Pin_18, 5V_DC_Fan.5V
  N2: NodeMCU_ESP32.Pin_19, BME280_Breakout.VIN
  N3: NodeMCU_ESP32.Pin_32, BME280_Breakout.SDA
  N4: NodeMCU_ESP32.Pin_35, BME280_Breakout.SCL

custom parts:
  ESP32 DOIT DEVKIT V1 36pin: ESP32 DOIT DEVKIT V1 36pin.
  Small Fan, based on Fan - Ventilador: Small 2-pin fan, commonly used with single-board computers, 3d-printers, etc. This work is based on a much larger fan, as commonly found in desktop computers
  BME280: Temperature Humidity Barometric presure Sensor
